# Fritzing sketch wheater (saved by Fritzing 0.9.2b)
breadboards: 1

parts:
  Part1 = Arduino Uno (Rev3)
  T1 = LM35 Temperature Sensor [package="TO92 [THT]"]
  R1 = Resistor [tolerance=±5% resistance=4.7k package=THT]
  RHT1 = Humidity and Temperature Sensor RHT03
  R2 = Resistor [tolerance=±5% resistance=10k package=THT]
  U1 = HIH-4030 [package=hih-4030]
  R3 = Photocell (LDR) [package=THT]
  R4 = Resistor [tolerance=±5% resistance=10k package=THT]
  Part15 = FC-28 Soil Hygrometer Module - Probe
  Part16 = FC-28 Soil Hygrometer Module
  Part17 = Barometric Pressure Sensor - BMP085 Breakout  # not connected

nets:
  N1: Part1.A0, U1.OUT
  N2: Part1.A1, R3.pin_1, R4.Pin_0
  N3: Part1.A2, Part16.AO
  N4: Part1.D2, T1.Vout, R1.Pin_0
  N5: Part1.D3_PWM, RHT1.Data-signal, R2.Pin_1
  3V3: Part1.3V3, Part16.VCC
  VCC: Part1.5V, T1.+Vs, R1.Pin_1, RHT1.Vcc, R2.Pin_0, U1.VCC, R4.Pin_1
  GND: Part1.GND, T1.GND, RHT1.GND_2, U1.GND, R3.pin_0, Part16.GND
  N6: Part15.POS, Part16.POS
  N7: Part15.NEG, Part16.NEG

custom parts:
  FC-28 Soil Hygrometer Module - Probe: The FC-28 is a soil hygrometer module that uses the Texas Instruments LM393 comparator chip to provide an analog measurement of soil humidity.
  FC-28 Soil Hygrometer Module: The FC-28 is a soil hygrometer module that uses the Texas Instruments LM393 comparator chip to provide an analog measurement of soil humidity. The digital output is high when soil moisture is over a certain threshold, as determined by adjusting the potentiometer.
